# Fritzing sketch ambilight (saved by Fritzing 0.9.3b)
breadboards: 1

parts:
  Raspberry_Pi_Zero1 = Raspberry Pi Zero
  V1 = DC Power [voltage=5]
  S_ONOFF = Round Pushbutton
  3V5VLevelShift = Logic Level Converter
  LedStrip_Main = ws2812b [package=THT]
  Mod1 = KY-019 5V Relay Module [package="Breakout board"]
  LED_ONOFF = LED - 3mm [color="White (4500K)" package="3 mm [THT]"]
  R1 = Resistor [tolerance=±5% resistance=330 package=THT]
  LedStrip_Base = ws2812b [package=THT]

nets:
  3V3: Raspberry_Pi_Zero1.3v3, Raspberry_Pi_Zero1.3V3, 3V5VLevelShift.LV
  N1: Raspberry_Pi_Zero1.GPIO3, S_ONOFF.leg1
  N2: Raspberry_Pi_Zero1.GIPO13, 3V5VLevelShift.TX2_LV
  GND: Raspberry_Pi_Zero1.GND, V1.V-, S_ONOFF.leg0, 3V5VLevelShift.GND, LedStrip_Main.VSS, Mod1.-, LED_ONOFF.cathode, LedStrip_Base.VSS
  N3: Raspberry_Pi_Zero1.GIPO24, Mod1.S
  N4: Raspberry_Pi_Zero1.GIPO23, R1.Pin_0
  N5: Raspberry_Pi_Zero1.GIPO18, 3V5VLevelShift.TX_LV
  N6: Raspberry_Pi_Zero1.5V, V1.V+, 3V5VLevelShift.HV, Mod1.+, Mod1.Common
  N7: 3V5VLevelShift.TX_HV, LedStrip_Main.DIN
  N8: 3V5VLevelShift.TX2_HV, LedStrip_Base.DIN
  VDD: LedStrip_Main.VDD, Mod1.NO, LedStrip_Base.VDD
  N9: LED_ONOFF.anode, R1.Pin_1

custom parts:
  KY-019 5V Relay Module: KY-019 5V Relay module, used to control AC circuits. (Special thanks to vanepp for fixing the PCB holes and other errors)
